# Fritzing sketch schematics_v2 (saved by Fritzing 0.9.3b)
circuit board: 8.46667cm x 5.64444cm
breadboards: 1

parts:
  U1 = NodeMCU V1.0
  PIR1 = PIR sensor
  VCC1 = Battery block 9V
  LED1 = smd LED [color="Red (633nm)" package="0805 [SMD]"]
  J1 = Basic Servo
  R1 = Resistor [tolerance=±5% resistance=220 package=THT]
  S1 = Pushbutton [package="[THT]"]

nets:
  N1: U1.D0, R1.Pin_1
  N2: U1.D1, S1.Pin_3, S1.Pin_4
  N3: U1.3V3, PIR1.SIG
  GND: U1.GND, PIR1.GND, VCC1.-, J1.gnd
  VIN: U1.Vin, PIR1.VDD, VCC1.+, J1.vcc
  N4: U1.A0, J1.pulse
  N5: LED1.cathode, S1.Pin_1, S1.Pin_2
  N6: LED1.anode, R1.Pin_0

custom parts:
  NodeMCU V1.0: ESP8266 based NodeMCU
